# Fritzing sketch Circuitry (saved by Fritzing 1.0.4)
breadboards: 1

parts:
  A1 = 5 channel TCRT5000 line tracker
  Part1 = Arduino Uno (Rev3) - ICSP
  L298N2 = L298N DC motor driver
  HC-SR04_Sensor_1 = HC-SR04 Ultrasonic Distance Sensor
  M1 = DC Motor [voltage_(max)=6V voltage_(min)=3V]
  M2 = DC Motor [voltage_(max)=6V voltage_(min)=3V]
  U1 = SWITCH-SPST-2 [package=switch-spst-vertical]
  VCC1 = 4 x AAA Battery Mount [internal_resistance=0.1Ω]
  J1 = Basic Servo

nets:
  N1: A1.Pin_1, Part1.A4/SDA
  N2: A1.Pin_2, Part1.A3
  N3: A1.Pin_3, Part1.A2
  N4: A1.Pin_4, Part1.A1
  N5: A1.Pin_5, Part1.A0
  GND: A1.Pin_7, Part1.GND, L298N2.GND, HC-SR04_Sensor_1.GND, VCC1.-, J1.gnd
  N6: Part1.D8, L298N2.IN3
  N7: Part1.D9_PWM, L298N2.ENA
  N8: Part1.D10_PWM/SS, L298N2.ENB
  N9: Part1.D12/MISO, HC-SR04_Sensor_1.ECHO
  N10: Part1.D13/SCK, HC-SR04_Sensor_1.TRIG
  N11: Part1.D3_PWM, J1.pulse
  N12: Part1.D4, L298N2.IN4
  N13: Part1.D6_PWM, L298N2.IN1
  N14: Part1.D7, L298N2.IN2
  5V: Part1.5V, HC-SR04_Sensor_1.VCC
  VIN: Part1.VIN, L298N2.12V, U1.P
  N15: L298N2.OUT1, M1.pin_2
  N16: L298N2.OUT2, M1.pin_1
  N17: L298N2.OUT3, M2.pin_1
  N18: L298N2.OUT4, M2.pin_2
  N19: U1.O, VCC1.+

custom parts:
  L298N DC motor driver: 2x DC motor driver with 78M05 positive voltage regulator (7..35 V) L298N: max 46 V, 2 A Set 5 V Enable jumper to enable 5 V regultor (needed for the L298N) and +5 V output at screw terminal or supply external +5 V at screw terminal Set ENA and/or ENB to +5 V to enable motor permanently or supply ENA and/or ENB with PWM signal IN1 and IN2 set rotation directory for motor A (OUT1/OUT2) IN2 and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
